# Fritzing sketch Schematic (saved by Fritzing 0.9.3b)
breadboards: 1

parts:
  V1_35A_Supply = DC Power [voltage=12V]
  Part2 = Arduino Mega 2560 (Rev3)
  D1 = Rectifier Diode [part_number=FFH50US60S_F085 package="300 mil [THT]"]
  D2 = Rectifier Diode [part_number=1N4001 package="300 mil [THT]"]
  R1 = Resistor [tolerance=±5% resistance=2.2k package=THT]
  R2 = Resistor [tolerance=±5% resistance=1k package=THT]
  C1 = Electrolytic Capacitor [capacitance=470µF package="100 mil [THT, electrolytic]"]  # not connected
  LED1_Status = LED - 5mm [color="Yellow (595nm)" package="5 mm [THT]"]
  S1_Manual_Upper = Toggle Switch [package=THT]
  Regulator = mystery part, 3 pins [chip_label=SWADJ3]
  Fuse1 = Fuse with Handler [part_number="3 A"]
  Fuse2 = Fuse with Handler [part_number=15A]
  TMP = TEMPERATURE-SENSOR [part_number=" TMP36" package=to-92]
  T2_Upper_Motor = Screw terminal - 2 pins [package=THT]
  T3_Lower_Motor = Screw terminal - 2 pins [package=THT]
  T1_PowerIn = Screw terminal - 2 pins [package=THT]
  Monster_Moto_Shield = Arduino Motor Shield (Rev3)
  M1_Upper_Motor = DC Motor
  M2_Lower_Motor = DC Motor
  R3 = Resistor [tolerance=±5% resistance=1k package=THT]
  LED2_Lower_Open = LED - 5mm [color="Red (633nm)" package="5 mm [THT]"]
  LED3_Upper_Open = LED - 5mm [color="Red (633nm)" package="5 mm [THT]"]
  LED4_Opening = LED - 5mm [color="Red (633nm)" package="5 mm [THT]"]
  LED5_Opening = LED - 5mm [color="Red (633nm)" package="5 mm [THT]"]
  LED6_Closing = LED - 5mm [color="Green (570nm)" package="5 mm [THT]"]
  LED7_Closing = LED - 5mm [color="Green (570nm)" package="5 mm [THT]"]
  LED8_Closed = LED - 5mm [color="Green (570nm)" package="5 mm [THT]"]
  LED9_Closed = LED - 5mm [color="Green (570nm)" package="5 mm [THT]"]
  R4 = Resistor [tolerance=±5% resistance=1k package=THT]
  S1_Manual_Lower = Toggle Switch [package=THT]
  S1-NC_Upper_Open = Reed switch [package=THT]
  S2-NC_Upper_Closed = Reed switch [package=THT]
  S3-NC_Lower_Open = Reed switch [package=THT]
  S4-NC_Lower_Closed = Reed switch [package=THT]

nets:
  N1: V1_35A_Supply.V+, D1.anode
  N2: Part2.A8, R2.Pin_0
  N3: Part2.A10, TMP.ADJ
  N4: Part2.SDA, LED1_Status.anode
  5V: Part2.5V, TMP.VCC
  N5: Part2.VIN, Fuse1.Connector2
  N6: Part2.D22, S1-NC_Upper_Open.pin_2
  N7: Part2.D23, S2-NC_Upper_Closed.pin_2
  N8: Part2.D24, S3-NC_Lower_Open.pin_2
  N9: Part2.D25, S4-NC_Lower_Closed.pin_2
  N10: Part2.D26, LED3_Upper_Open.anode
  N11: Part2.D27, LED8_Closed.anode
  N12: Part2.D28, LED2_Lower_Open.anode
  N13: Part2.D29, LED9_Closed.anode
  N14: Part2.D32, LED4_Opening.anode
  N15: Part2.D33, LED6_Closing.anode
  N16: Part2.D34, LED5_Opening.anode
  N17: Part2.D35, LED7_Closing.anode
  N18: Part2.D38, S1_Manual_Upper.L2
  N19: Part2.D39, S1_Manual_Upper.L1
  N20: Part2.D40, S1_Manual_Lower.L2
  N21: Part2.D41, S1_Manual_Lower.L1
  N22: Part2.D45, Monster_Moto_Shield.D5_PWM
  N23: D2.anode, R1.Pin_0, Fuse2.Connector2, T1_PowerIn.pin2
  N24: LED1_Status.cathode, R3.Pin_0, LED2_Lower_Open.cathode, LED3_Upper_Open.cathode, LED4_Opening.cathode, LED5_Opening.cathode
  GND: S1_Manual_Upper.COM, TMP.GND, S1_Manual_Lower.COM, S1-NC_Upper_Open.pin_1, S2-NC_Upper_Closed.pin_1, S3-NC_Lower_Open.pin_1, S4-NC_Lower_Closed.pin_1
  N25: Regulator.pin1, Fuse1.Connector1
  N26: T2_Upper_Motor.pin1, M1_Upper_Motor.pin_2
  N27: T2_Upper_Motor.pin2, M1_Upper_Motor.pin_1
  N28: T3_Lower_Motor.pin1, M2_Lower_Motor.pin_2
  N29: T3_Lower_Motor.pin2, M2_Lower_Motor.pin_1
  N30: LED6_Closing.cathode, LED7_Closing.cathode, LED8_Closed.cathode, LED9_Closed.cathode, R4.Pin_0

notes:
  Shutter Controller, Replacement for Foster Shutter Controller, 2.0
