# Fritzing sketch SpinDomeSchematic (saved by Fritzing 0.9.3b)
breadboards: 1

parts:
  V1_35A_Supply = DC Power [voltage=12V]
  D1 = Rectifier Diode [package="300 mil [THT]"]
  Fuse1 = Fuse with Handler [part_number=15A]  # not connected
  T2_Not_Used = Screw terminal - 2 pins [package=THT]  # not connected
  T1_Motor = Screw terminal - 2 pins [package=THT]
  Monster_Moto_Shield = Arduino Motor Shield (Rev3)
  R3 = Resistor [tolerance=±5% resistance=1k package=THT]
  LED_Rotation_Status = LED - 5mm [color="White (6500K)" package="5 mm [THT]"]
  LED_Home = LED - 5mm [color="Green (555nm)" package="5 mm [THT]"]  # not connected
  R4_BiColor = Resistor [tolerance=±5% resistance=330 package=THT]
  S1_Manual_Rotate = Toggle Switch [package=THT]
  S1-Home_Switch = Reed switch [package=THT]
  Arduino_Uno = Arduino Uno (Rev3)
  M1_Upper_Motor = DC Motor
  LED_IR_Emitter = LED - 5mm [color="Infrared (850nm)" package="5 mm [THT]"]
  LED_Detector = LED - 5mm [color="White (4500K)" package="5 mm [THT]"]
  R6 = Resistor [tolerance=±5% resistance=220 package=THT]
  R7 = Resistor [tolerance=±5% resistance=4.7k package=THT]
  U1_555_Timer = 555 Timer [package="DIP8 [THT]"]
  IC1_741_Op_Amp = IC, DIP package, 8 pins [chip_label=741]
  C1 = Ceramic Capacitor [capacitance=100nF package="100 mil [THT, multilayer]"]
  LED_Sig = LED - 5mm [color="Red (660nm)" package="5 mm [THT]"]
  R8 = Resistor [tolerance=±5% resistance=1k package=THT]
  R9 = Resistor [tolerance=±5% resistance=330k package=THT]
  R10 = Resistor [tolerance=±5% resistance=3.3k package=THT]
  R11 = Resistor [tolerance=±5% resistance=1k package=THT]
  C2 = Ceramic Capacitor [capacitance=100nF package="100 mil [THT, multilayer]"]
  R12 = Resistor [tolerance=±5% resistance=100k package=THT]
  D2 = Rectifier Diode [part_number=1N4001 package="300 mil [THT]"]
  LED_Tic = LED - 5mm [color="Red (633nm)" package="5 mm [THT]"]  # not connected
  R13 = Resistor [tolerance=±5% resistance=1k package=THT]  # not connected
  S1 = Toggle Switch [package=THT]

nets:
  N1: V1_35A_Supply.V+, D1.anode
  N2: V1_35A_Supply.V-, Monster_Moto_Shield.B-
  N3: T1_Motor.pin1, M1_Upper_Motor.pin_2
  N4: T1_Motor.pin2, M1_Upper_Motor.pin_1
  N5: R3.Pin_0, Arduino_Uno.D12/MISO
  N6: LED_Rotation_Status.anode, Arduino_Uno.A4/SDA
  N7: R4_BiColor.Pin_1, Arduino_Uno.A5/SCL
  N8: S1_Manual_Rotate.L1, Arduino_Uno.D10_PWM/SS
  GND: S1_Manual_Rotate.COM, S1-Home_Switch.pin_2, Arduino_Uno.GND, LED_IR_Emitter.cathode, U1_555_Timer.Ground, C1.0, R8.Pin_1
  N9: S1_Manual_Rotate.L2, Arduino_Uno.D11_PWM/MOSI
  N10: S1-Home_Switch.pin_1, Arduino_Uno.D3_PWM
  N11: Arduino_Uno.D2, U1_555_Timer.Output, S1.COM
  N12: Arduino_Uno.5V, D2.cathode
  N13: LED_IR_Emitter.anode, R6.Pin_1
  N14: LED_Detector.anode, R7.Pin_1
  N15: R6.Pin_0, R7.Pin_0, U1_555_Timer.Reset, U1_555_Timer.Vcc_Supply_Voltage, IC1_741_Op_Amp.pin7, D2.anode
  N16: U1_555_Timer.Trigger, U1_555_Timer.Threshold, IC1_741_Op_Amp.pin6, R9.Pin_1
  N17: IC1_741_Op_Amp.pin2, R9.Pin_0, R12.Pin_1
  N18: IC1_741_Op_Amp.pin4, R10.Pin_1
  N19: LED_Sig.anode, S1.L2
  N20: R10.Pin_0, R11.Pin_1, C2.1, R12.Pin_0

notes:
  Rotation Controller, Replacement for Foster Rotation Controller, 2.0
  BrewSpinDome Rotation Sensor, Separate PCB for sensor
