# Fritzing sketch SpinDomeWiringPlan (saved by Fritzing 0.9.3b)
circuit board: 8.46667cm x 5.64444cm
perfboards: 2

parts:
  Part4 = Arduino Motor Shield
  J1_MonsterMoto_Power = Screw terminal - 2 pins [package=THT]
  15Amp_BigFuse = Fuse with Handler [part_number=Htc-15m]
  S1_Manual_Switch = Toggle Switch [package=THT]
  VCC1 = Battery block 9V
  D4 = Rectifier Diode [part_number=FFH50US60S_F085 package="300 mil [THT]"]
  J1_Home_Switch = RJ9 [package=rj9]
  Part5 = Arduino Uno (Rev3)  # not connected
  R17 = Resistor [tolerance=±5% resistance=1k package=THT]
  LED_Home = LED - 5mm [color="Green (555nm)" package="5 mm [THT]"]
  J2_IR_Sensor = RJ11 Jack [package=rj11-6]
  R19 = Resistor [tolerance=±5% resistance=330 package=THT]
  LED_East/West_Move1 = LED - 5mm [color="Orange (612nm)" package="5 mm [THT]"]
  J14_Bundle_2 = female alternating pin header, 4 pins [form="♀ (female)"]
  J14_Bundle1 = female pin header, 4 pins [form="♀ (female)"]
  J14_PCB_Signals11 = female alternating pin header, 4 pins [form="♀ (female)"]  # not connected
  J14_Bundle3 = female alternating pin header, 4 pins [form="♀ (female)"]
  J14_PCB_Signals10 = female pin header, 6 pins [form="♀ (female)"]
  IC1_Op_Amp1 = IC, DIP package, 8 pins [chip_label="741 "]
  IC2_556 = IC, DIP package, 8 pins [chip_label=555]
  R27_to_emitter = Resistor [tolerance=±5% resistance=220 package=THT]
  R28_from_Detector = Resistor [tolerance=±5% resistance=4.7k package=THT]
  R29_Feed_OpAmp = Resistor [tolerance=±5% resistance=100k package=THT]
  R30_Upper_OpAmp = Resistor [tolerance=±5% resistance=1k package=THT]
  R32_Lower_OpAmp = Resistor [tolerance=±5% resistance=3.3k package=THT]
  R33 = Resistor [tolerance=±5% resistance=330k package=THT]
  C3_OpAmp = Ceramic Capacitor [capacitance=100nF package="100 mil [THT, multilayer]"]
  C4_Timer = Ceramic Capacitor [capacitance=100nF package="100 mil [THT, multilayer]"]
  IR_Emitter1 = LED - 5mm [color="Infrared (940nm)" package="5 mm [THT]"]
  IR_Detector1 = LED - 5mm [color="Infrared (850nm)" package="5 mm [THT]"]
  D5 = Rectifier Diode [part_number=1N4001 package="300 mil [THT]"]
  LED3_Tic_Bump = LED - 5mm [color="Red (633nm)" package="5 mm [THT]"]
  R34_Tic_LED = Resistor [tolerance=±5% resistance=470 package=THT]
  MainPlug = DB9 Connector [package=db9]
  MainCable = DB9 Connector [package=db9]
  J2 = female pin header, 10 pins [form="♀ (female)"]
  J3 = male pin header, 10 pins [form="♂ (male)"]
  LED_Tic = LED - 3mm [color="Red (635nm)" package="3 mm [THT]"]
  R36 = Resistor [tolerance=±5% resistance=1k package=THT]  # not connected
  J14_PCB_Signals13 = female pin header, 4 pins [form="♀ (female)"]

nets:
  N1: Part4.5V, J2_IR_Sensor.1, J14_Bundle1.pin3, J14_PCB_Signals13.pin1
  N2: Part4.A4, R19.Pin_1, J14_PCB_Signals10.pin2
  N3: Part4.A5, LED_East/West_Move1.anode, J14_Bundle_2.pin2, J14_PCB_Signals10.pin6
  N4: Part4.D2, J2_IR_Sensor.5, J14_Bundle1.pin2, J14_PCB_Signals13.pin3
  N5: Part4.D3, J1_Home_Switch.3, J14_Bundle1.pin1, J14_PCB_Signals13.pin2
  N6: Part4.D10, S1_Manual_Switch.L2, J14_Bundle3.pin2, J14_PCB_Signals10.pin4
  N7: Part4.D11, S1_Manual_Switch.L1, J14_Bundle3.pin1, J14_PCB_Signals10.pin5
  N8: Part4.D12, R17.Pin_1, J14_PCB_Signals10.pin3
  N9: Part4.GND, S1_Manual_Switch.COM, LED_Home.cathode, J14_Bundle3.pin4, J14_PCB_Signals10.pin1
  N10: J1_MonsterMoto_Power.pin1, 15Amp_BigFuse.Connector2
  N11: J1_MonsterMoto_Power.pin2, VCC1.-
  N12: 15Amp_BigFuse.Connector1, D4.cathode
  N13: VCC1.+, D4.anode
  N14: J1_Home_Switch.1, J2_IR_Sensor.3, J14_Bundle1.pin4
  N15: LED_Home.anode, J14_Bundle_2.pin3
  N16: LED_East/West_Move1.cathode, J14_Bundle_2.pin1
  N17: J14_Bundle_2.pin4, LED_Tic.anode
  N18: IC1_Op_Amp1.pin2, R33.Pin_1
  N19: IC1_Op_Amp1.pin3, R28_from_Detector.Pin_1, J3.pin4
  N20: IC1_Op_Amp1.pin4, IC2_556.pin1, R32_Lower_OpAmp.Pin_1, C3_OpAmp.1, C4_Timer.1, R34_Tic_LED.Pin_1, J3.pin9, J3.pin10
  N21: IC1_Op_Amp1.pin6, IC2_556.pin2, IC2_556.pin6, R33.Pin_0
  N22: IC1_Op_Amp1.pin7, IC2_556.pin4, IC2_556.pin8, R27_to_emitter.Pin_0, R28_from_Detector.Pin_0, R30_Upper_OpAmp.Pin_0, D5.cathode
  N23: IC2_556.pin3, J3.pin5
  N24: IC2_556.pin5, C4_Timer.0
  N25: R27_to_emitter.Pin_1, J3.pin2
  N26: R29_Feed_OpAmp.Pin_1, R30_Upper_OpAmp.Pin_1, R32_Lower_OpAmp.Pin_0, C3_OpAmp.0
  N27: IR_Emitter1.anode, MainCable.2
  N28: IR_Detector1.cathode, MainCable.1
  N29: IR_Detector1.anode, MainCable.3
  N30: D5.anode, J3.pin1
  N31: LED3_Tic_Bump.cathode, J2.pin7
  N32: LED3_Tic_Bump.anode, J2.pin8
  N33: R34_Tic_LED.Pin_0, J3.pin8
  N34: MainPlug.2, J2.pin4
  N35: MainPlug.3, J2.pin2
  N36: MainPlug.4, J2.pin9
  N37: MainPlug.5, J2.pin10
  N38: MainPlug.7, J2.pin1
  N39: MainPlug.8, J2.pin3
  N40: MainPlug.9, J2.pin5

notes:
  Home Switch - yellow & red
  Normally closed
  RJ9
  Motor Board has 2 small LEDs for each motor.
  Right is East?, left is West?.
  Second Motor not used
  IR Sensor RJ11
  Wire:
  U - sensor out
  OW - Ground
  O - LED 5V
  Connection:
  Y - Sensor
  B - Ground
  G - 5V In
  Manual Rotate Switch
  Mark 2 Sensor Board
  Home
  Interrupt Tick
  Direction Indicator
  3 bundle
  1 bundle
  2 bundle
  Test Tic Sig
  Test Gnd
  Test Home
  Cable to Sensor
