# Fritzing sketch WiringPlan (saved by Fritzing 0.9.1b)
perfboards: 1

parts:
  Part4 = Arduino Motor Shield
  J1_MonsterMoto_Power = Screw terminal - 2 pins [package=THT]
  15Amp_BigFuse = Fuse with Handler [part_number=Htc-15m]
  S1_Manual_Switch = Toggle Switch [package=THT]
  VCC1 = Battery block 9V
  J14_PCB_Signals9 = female pin header, 8 pins [form="♀ (female)"]
  D4 = Rectifier Diode [part_number=FFH50US60S_F085 package="300 mil [THT]"]
  J1_Home_Switch = RJ9 [package=rj9]
  Part5 = Arduino Uno (Rev3)  # not connected
  R15_10K_Pot = Rotary Potentiometer (Small) [maximum_resistance=10kΩ package=THT]
  R16 = Resistor [tolerance=±5% resistance=470 package=THT]
  R17 = Resistor [tolerance=±5% resistance=1k package=THT]
  LED3_West_Move = LED - 5mm [color="Red (633nm)" package="5 mm [THT]"]
  J14_PCB_Signals10 = female pin header, 8 pins [form="♀ (female)"]
  LED5_East_Move = LED - 5mm [color="Orange (620nm)" package="5 mm [THT]"]
  R18 = Resistor [tolerance=±5% resistance=22k package=THT]
  U1 = mystery part, 4 pins [chip_label="IR Sensor"]
  J2_IR_Sensor = RJ11 Jack [package=rj11-6]
  U2_RJ11_Plug = mystery part, 6 pins [chip_label=RJ11]
  R19 = Resistor [tolerance=±5% resistance=330 package=THT]
  J14_PCB_Signals8 = female pin header, 8 pins [form="♀ (female)"]

nets:
  N1: Part4.5V, R15_10K_Pot.wiper, R16.Pin_0, J14_PCB_Signals10.pin1
  N2: Part4.A0, J14_PCB_Signals10.pin3, R19.Pin_1
  N3: Part4.A1, LED3_West_Move.anode, J14_PCB_Signals10.pin5, J14_PCB_Signals10.pin6
  N4: Part4.A2, J14_PCB_Signals9.pin6, J14_PCB_Signals9.pin7, LED5_East_Move.anode
  N5: Part4.D2, J14_PCB_Signals10.pin2, R18.Pin_1, J2_IR_Sensor.5
  N6: Part4.D3, J1_Home_Switch.3
  N7: Part4.D11, S1_Manual_Switch.L2
  N8: Part4.D12, S1_Manual_Switch.L1
  N9: Part4.GND, J14_PCB_Signals8.pin8
  N10: J1_MonsterMoto_Power.pin1, 15Amp_BigFuse.Connector2
  N11: J1_MonsterMoto_Power.pin2, VCC1.-
  N12: 15Amp_BigFuse.Connector1, D4.cathode
  N13: S1_Manual_Switch.COM, J14_PCB_Signals8.pin3
  N14: VCC1.+, D4.anode
  N15: J14_PCB_Signals9.pin4, J14_PCB_Signals9.pin5, J2_IR_Sensor.3
  N16: J14_PCB_Signals9.pin8, R17.Pin_1, LED5_East_Move.cathode
  N17: J1_Home_Switch.1, J1_Home_Switch.2, J14_PCB_Signals8.pin2
  N18: R16.Pin_1, J2_IR_Sensor.1
  N19: LED3_West_Move.cathode, J14_PCB_Signals10.pin4, R19.Pin_0
  N20: U1.pin1, U2_RJ11_Plug.pin1
  N21: U1.pin3, U2_RJ11_Plug.pin3
  N22: U1.pin4, U2_RJ11_Plug.pin5

notes:
  Home Switch - yellow & red
  Normally closed
  RJ9
  Motor Board has 2 small LEDs for each output motor.
  Upper Motor: Rt is close, left is open.
  Lower Motor: Rt is open, left is closed.
  Motor
  Second Motor not used
  IR Sensor RJ11
  Blue - sensor out
  O/W Ground
  O - LED 5V
  Manual Rotate Switch
